# Fritzing sketch esp32-MAX31855-Relay (saved by Fritzing 0.9.3b)
breadboards: 1

parts:
  Part3 = Adafruit Thermocouple Amplifier MAX31855 [part_number="Adafruit #269"]
  MH-ET_LIVE_ESP32_DEVKIT2 = MH-ET LIVE ESP32 DEVKIT 38 pins
  A2 = nozzle-bolt style thermocouple [package=THT]
  Relay_5V1 = Keyes Relay [package=THT]
  A3 = nozzle-bolt style thermocouple [package=THT]
  Power_plug1 = Power plug
  LED1 = RGB LED - (4 legs) [package="5 mm [THT]"]
  R1 = Resistor [tolerance=±5% resistance=220 package=THT]
  R2 = Resistor [tolerance=±5% resistance=220 package=THT]
  R3 = Resistor [tolerance=±5% resistance=220 package=THT]

nets:
  N1: Part3.THERMO-, A2.pin2
  N2: Part3.THERMO+, A2.pin1
  +3V3: Part3.+3V3, MH-ET_LIVE_ESP32_DEVKIT2.3V3
  GND: Part3.GND, MH-ET_LIVE_ESP32_DEVKIT2.GND, Relay_5V1.ground
  N3: Part3.DO, MH-ET_LIVE_ESP32_DEVKIT2.IO12
  N4: Part3.CS, MH-ET_LIVE_ESP32_DEVKIT2.IO13
  N5: Part3.CLK, MH-ET_LIVE_ESP32_DEVKIT2.IO14
  N6: MH-ET_LIVE_ESP32_DEVKIT2.5V, Relay_5V1.power
  N7: MH-ET_LIVE_ESP32_DEVKIT2.IO5, R1.Pin_1
  N8: MH-ET_LIVE_ESP32_DEVKIT2.IO17, LED1.common_anode
  N9: MH-ET_LIVE_ESP32_DEVKIT2.IO16, R2.Pin_1
  N10: MH-ET_LIVE_ESP32_DEVKIT2.IO4, R3.Pin_1
  N11: MH-ET_LIVE_ESP32_DEVKIT2.IO2, Relay_5V1.signal
  N12: Relay_5V1.C, Power_plug1.GND
  N13: Relay_5V1.NO, A3.pin1
  N14: A3.pin2, Power_plug1.VCC
  N15: LED1.red_cathode, R1.Pin_0
  N16: LED1.green_cathode, R2.Pin_0
  N17: LED1.blue_cathode, R3.Pin_0

notes:
  Soldering Iron
  AC Power Supply
  Thermocoupler K

custom parts:
  Adafruit Thermocouple Amplifier MAX31855: Thermocouples are very sensitive, requiring a good amplifier with a cold-compensation reference. The MAX31855K does everything for you, and can be easily interfaced with any microcontroller, even one without an analog input. This breakout board has the chip itself, a 3.3V regulator with 10uF bypass capacitors and level shifting circuitry, all assembled and tested. Comes with a 2 pin terminal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
  MH-ET LIVE ESP32 DEVKIT 38 pins: http://mh.nodebb.com/topic/2/mh-et-live-esp32-devkit
  nozzle-bolt style thermocouple: Generic nozzle-bolt style thermocouple.
  Keyes Relay: The Keyes 5V relay module is suitable for SCM development, home appliance control. It uses a 5V~12V TIL control signal which can control DC / AC signal.
