# Fritzing sketch esp32-OPT3001 (saved by Fritzing 0.9.3b)

parts:
  VCC1 = Battery block 9V
  U1 = Voltage Regulator [package=to220-adj]
  R2 = Resistor [tolerance=±5% resistance=10 package=THT]  # not connected
  Power_RGB1 = Prolight RGB 3 Watt Star
  Q1 = NPN-Transistor [package="SOT-23 [SMD]"]
  R3 = Resistor [tolerance=±5% resistance=4.7 package=THT]  # not connected
  MH-ET_LIVE_ESP32_DEVKIT1 = MH-ET LIVE ESP32 DEVKIT 38 pins
  R1 = Resistor [tolerance=±5% resistance=10 package=THT]
  Mod1 = CJMCU-3001

nets:
  GND: VCC1.-, MH-ET_LIVE_ESP32_DEVKIT1.GND, Mod1.GND
  N1: U1.ADJ, R1.Pin_0
  N2: U1.IN, Power_RGB1.B+
  N3: Power_RGB1.B-, Q1.1
  N4: Q1.0, MH-ET_LIVE_ESP32_DEVKIT1.IO15
  3V3: MH-ET_LIVE_ESP32_DEVKIT1.3V3, Mod1.VCC
  N5: MH-ET_LIVE_ESP32_DEVKIT1.IO22, Mod1.SCL
  N6: MH-ET_LIVE_ESP32_DEVKIT1.TXD0, Mod1.SDA

notes:
  CJMCU-3001
  2N2222A
  LM317
  R1=10Ohm
  R2=14.7Ohm

custom parts:
  MH-ET LIVE ESP32 DEVKIT 38 pins: http://mh.nodebb.com/topic/2/mh-et-live-esp32-devkit
