# Fritzing sketch esp32-led-source-sink (saved by Fritzing 0.9.3b)

parts:
  MH-ET_LIVE_ESP32_DEVKIT1 = MH-ET LIVE ESP32 DEVKIT 38 pins
  LED1 = LED - 3mm [color="Red (633nm)" package="3 mm [THT]"]
  R1 = Resistor [tolerance=±5% resistance=220 package=THT]
  LED2 = LED - 3mm [color="Red (633nm)" package="3 mm [THT]"]
  R2 = Resistor [tolerance=±5% resistance=220 package=THT]

nets:
  N1: MH-ET_LIVE_ESP32_DEVKIT1.3V3, R2.Pin_1
  N2: MH-ET_LIVE_ESP32_DEVKIT1.IO12, LED2.cathode
  N3: MH-ET_LIVE_ESP32_DEVKIT1.IO13, R1.Pin_1
  N4: MH-ET_LIVE_ESP32_DEVKIT1.GND, LED1.cathode

custom parts:
  MH-ET LIVE ESP32 DEVKIT 38 pins: http://mh.nodebb.com/topic/2/mh-et-live-esp32-devkit
