# Fritzing sketch esp32-line-following-robot (saved by Fritzing 0.9.3b)

parts:
  S2 = H-Bridge with L298N
  MH-ET_LIVE_ESP32_DEVKIT2 = MH-ET LIVE ESP32 DEVKIT 38 pins
  M3 = DC Motor
  M4 = DC Motor
  U3 = TCRT5000 Line Tracker
  U4 = TCRT5000 Line Tracker

nets:
  N1: S2.ENA, MH-ET_LIVE_ESP32_DEVKIT2.IO19
  N2: S2.IN1, MH-ET_LIVE_ESP32_DEVKIT2.IO18
  N3: S2.IN2, MH-ET_LIVE_ESP32_DEVKIT2.IO5
  N4: S2.IN3, MH-ET_LIVE_ESP32_DEVKIT2.IO12
  N5: S2.IN4, MH-ET_LIVE_ESP32_DEVKIT2.IO14
  N6: S2.ENB, MH-ET_LIVE_ESP32_DEVKIT2.IO13
  N7: S2.M1-01, M3.pin_1
  N8: S2.M1-02, M3.pin_2
  N9: S2.M2-01, M4.pin_2
  N10: S2.M2-02, M4.pin_1
  N11: MH-ET_LIVE_ESP32_DEVKIT2.IO4, U3.Do
  N12: MH-ET_LIVE_ESP32_DEVKIT2.IO0, U4.Do

custom parts:
  H-Bridge with L298N: h-bridge
  MH-ET LIVE ESP32 DEVKIT 38 pins: http://mh.nodebb.com/topic/2/mh-et-live-esp32-devkit
  TCRT5000 Line Tracker: A line tracker module based on TCRT5000 (Vishay)
