# Fritzing sketch esp32-LM298N (saved by Fritzing 0.9.3b)

parts:
  S1 = H-Bridge with L298N
  MH-ET_LIVE_ESP32_DEVKIT1 = MH-ET LIVE ESP32 DEVKIT 38 pins
  M1 = DC Motor
  M2 = DC Motor

nets:
  N1: S1.ENA, MH-ET_LIVE_ESP32_DEVKIT1.IO19
  N2: S1.IN1, MH-ET_LIVE_ESP32_DEVKIT1.IO18
  N3: S1.IN2, MH-ET_LIVE_ESP32_DEVKIT1.IO5
  N4: S1.IN3, MH-ET_LIVE_ESP32_DEVKIT1.IO12
  N5: S1.IN4, MH-ET_LIVE_ESP32_DEVKIT1.IO14
  N6: S1.ENB, MH-ET_LIVE_ESP32_DEVKIT1.IO13
  N7: S1.M1-01, M2.pin_1
  N8: S1.M1-02, M2.pin_2
  N9: S1.M2-01, M1.pin_2
  N10: S1.M2-02, M1.pin_1

custom parts:
  H-Bridge with L298N: h-bridge
  MH-ET LIVE ESP32 DEVKIT 38 pins: http://mh.nodebb.com/topic/2/mh-et-live-esp32-devkit
