# Fritzing sketch esp32_pull-up-down-resistor (saved by Fritzing 0.9.3b)

parts:
  R2 = Resistor [tolerance=±5% resistance=220 package=THT]
  MH-ET_LIVE_ESP32_DEVKIT2 = MH-ET LIVE ESP32 DEVKIT 38 pins
  S2 = Pushbutton [package="[THT]"]
  R3 = Resistor [tolerance=±5% resistance=220 package=THT]
  S3 = Pushbutton [package="[THT]"]

nets:
  N1: R2.Pin_0, MH-ET_LIVE_ESP32_DEVKIT2.5V, S3.Pin_3, S3.Pin_4
  N2: R2.Pin_1, MH-ET_LIVE_ESP32_DEVKIT2.IO15, S2.Pin_3, S2.Pin_4
  N3: MH-ET_LIVE_ESP32_DEVKIT2.GND, S2.Pin_1, S2.Pin_2, R3.Pin_1
  N4: MH-ET_LIVE_ESP32_DEVKIT2.IO4, R3.Pin_0, S3.Pin_1, S3.Pin_2

custom parts:
  MH-ET LIVE ESP32 DEVKIT 38 pins: http://mh.nodebb.com/topic/2/mh-et-live-esp32-devkit
