# Fritzing sketch esp32-relay (saved by Fritzing 0.9.3b)

parts:
  MH-ET_LIVE_ESP32_DEVKIT1 = MH-ET LIVE ESP32 DEVKIT 38 pins
  U1 = 4-Channel 5v Relay Shield [package=relay-4ch5v10a]

nets:
  N1: MH-ET_LIVE_ESP32_DEVKIT1.IO25, U1.IN2
  N2: MH-ET_LIVE_ESP32_DEVKIT1.IO26, U1.IN3
  N3: MH-ET_LIVE_ESP32_DEVKIT1.IO27, U1.IN4
  5V: MH-ET_LIVE_ESP32_DEVKIT1.5V, U1.VCC
  GND: MH-ET_LIVE_ESP32_DEVKIT1.GND, U1.GND
  N4: MH-ET_LIVE_ESP32_DEVKIT1.IO2, U1.IN1

custom parts:
  MH-ET LIVE ESP32 DEVKIT 38 pins: http://mh.nodebb.com/topic/2/mh-et-live-esp32-devkit
  4-Channel 5v Relay Shield: 4 Channel 5v Relay Shield w. 2x SPD-06VDC-SD-C
