# Fritzing sketch esp32_LM35 (saved by Fritzing 0.9.3b)

parts:
  T1 = LM35 Temperature Sensor [package="TO92 [THT]"]
  MH-ET_LIVE_ESP32_DEVKIT1 = MH-ET LIVE ESP32 DEVKIT 38 pins

nets:
  N1: T1.+Vs, MH-ET_LIVE_ESP32_DEVKIT1.3V3
  N2: T1.Vout, MH-ET_LIVE_ESP32_DEVKIT1.IO34
  GND: T1.GND, MH-ET_LIVE_ESP32_DEVKIT1.GND

custom parts:
  MH-ET LIVE ESP32 DEVKIT 38 pins: http://mh.nodebb.com/topic/2/mh-et-live-esp32-devkit
