# Fritzing sketch esp32_MAX31855 (saved by Fritzing 0.9.3b)

parts:
  Part2 = Adafruit Thermocouple Amplifier MAX31855 [part_number="Adafruit #269"]
  MH-ET_LIVE_ESP32_DEVKIT1 = MH-ET LIVE ESP32 DEVKIT 38 pins
  A1 = nozzle-bolt style thermocouple [package=THT]

nets:
  N1: Part2.THERMO-, A1.pin2
  N2: Part2.THERMO+, A1.pin1
  +3V3: Part2.+3V3, MH-ET_LIVE_ESP32_DEVKIT1.3V3
  GND: Part2.GND, MH-ET_LIVE_ESP32_DEVKIT1.GND
  N3: Part2.DO, MH-ET_LIVE_ESP32_DEVKIT1.IO12
  N4: Part2.CS, MH-ET_LIVE_ESP32_DEVKIT1.IO13
  N5: Part2.CLK, MH-ET_LIVE_ESP32_DEVKIT1.IO14

custom parts:
  Adafruit Thermocouple Amplifier MAX31855: Thermocouples are very sensitive, requiring a good amplifier with a cold-compensation reference. The MAX31855K does everything for you, and can be easily interfaced with any microcontroller, even one without an analog input. This breakout board has the chip itself, a 3.3V regulator with 10uF bypass capacitors and level shifting circuitry, all assembled and tested. Comes with a 2 pin terminal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
  MH-ET LIVE ESP32 DEVKIT 38 pins: http://mh.nodebb.com/topic/2/mh-et-live-esp32-devkit
  nozzle-bolt style thermocouple: Generic nozzle-bolt style thermocouple.
