# Fritzing sketch esp32_thermistor (saved by Fritzing 0.9.3b)

parts:
  R1 = Temperature Sensor (Thermistor) [thermistor_type=NTC package=THT]
  MH-ET_LIVE_ESP32_DEVKIT1 = MH-ET LIVE ESP32 DEVKIT 38 pins
  R2 = Resistor [tolerance=±5% resistance=1k package=THT]

nets:
  N1: R1.pin_1, MH-ET_LIVE_ESP32_DEVKIT1.GND
  N2: MH-ET_LIVE_ESP32_DEVKIT1.3V3, R2.Pin_0
  N3: MH-ET_LIVE_ESP32_DEVKIT1.IO34, R2.Pin_1

notes:
  1kOhm
  TTC102

custom parts:
  MH-ET LIVE ESP32 DEVKIT 38 pins: http://mh.nodebb.com/topic/2/mh-et-live-esp32-devkit
